# Fritzing sketch Untitled Sketch (saved by Fritzing 0.9.3b)
breadboards: 1

parts:
  부품1 = Arduino Uno (Rev3) - ICSP
  hc-sr1 = hc-sr04
  J1 = Basic Servo

nets:
  GND: 부품1.GND, hc-sr1.GND, J1.gnd
  N1: 부품1.D2, hc-sr1.Trig
  N2: 부품1.D3_PWM, hc-sr1.Echo
  N3: 부품1.D4, J1.pulse
  VCC: 부품1.5V, hc-sr1.VCC, J1.vcc
